# Fritzing sketch 2015-05-22-leds_adressables (saved by Fritzing 0.9.2b)
breadboards: 1

parts:
  LED1 = RGB LED - (4 legs) [package="5 mm [THT]"]
  R1 = Resistor [tolerance=±5% resistance=220 package=THT]
  C3 = Ceramic Capacitor [capacitance="100 nF" package="0603 [SMD, multilayer]"]
  LED2 = RGB LED - (4 legs) [package="5 mm [THT]"]
  LED3 = RGB LED - (4 legs) [package="5 mm [THT]"]
  LED4 = RGB LED - (4 legs) [package="5 mm [THT]"]
  C4 = Ceramic Capacitor [capacitance="100 nF" package="0603 [SMD, multilayer]"]
  C5 = Ceramic Capacitor [capacitance="100 nF" package="0603 [SMD, multilayer]"]
  C6 = Ceramic Capacitor [capacitance="100 nF" package="0603 [SMD, multilayer]"]
  R2 = Resistor [tolerance=±5% resistance=220 package=THT]
  R3 = Resistor [tolerance=±5% resistance=220 package=THT]
  R4 = Resistor [tolerance=±5% resistance=220 package=THT]
  Nano1 = Arduino Nano v2.3

nets:
  N1: LED1.red_cathode, LED2.blue_cathode
  N2: LED1.common_anode, C3.0, LED2.common_anode, LED3.common_anode, LED4.red_cathode, LED4.common_anode, C4.0, C5.0, C6.0, Nano1.GND
  N3: LED1.green_cathode, R1.Pin_1, C3.1
  N4: LED1.blue_cathode, Nano1.D5
  N5: R1.Pin_0, R2.Pin_0, R3.Pin_0, R4.Pin_0, Nano1.+5V
  N6: LED2.red_cathode, LED3.blue_cathode
  N7: LED2.green_cathode, C4.1, R2.Pin_1
  N8: LED3.red_cathode, LED4.blue_cathode
  N9: LED3.green_cathode, C5.1, R4.Pin_1
  N10: LED4.green_cathode, C6.1, R3.Pin_1
